# Fritzing sketch Cicuit diagram (saved by Fritzing 1.0.6)
breadboards: 1

parts:
  U1 = LCD-16X2 [package=lcd-16x2]
  J1 = Basic Servo  # not connected
  Part1 = Arduino Uno (Rev3)  # not connected
  R1 = Photocell (LDR) [power=0.25W dark_resistance_@0.01lx=300kΩ light_resistance_@100lx=400Ω luminance=10lx package=THT]
  R2 = Resistor [tolerance=±5% resistance=1k package="1206 [SMD]"]
  R3 = Resistor [tolerance=±5% resistance=10k package="1206 [SMD]"]
  LED1 = LED - 5mm [color="Red (633nm)" current=0.030A package="5 mm [THT]"]

nets:
  N1: U1.DB7, R1.pin_0
  N2: U1.A, R3.Pin_1, LED1.cathode
  N3: R1.pin_1, R3.Pin_0
  N4: R2.Pin_1, LED1.anode
